// Digital circuit DRAM_Master.dig as structural Verilog
module DRAM_Master (
  input  clk,
  input  CTRL_DRAM__Read___Write,
  input  [1:0] CTRL_PC__Inc___Write___Reset,
  input  [3:0] Manual_Address_Input_PC,
  input  Chip_Select__IR___GPR,
  input  CTRL_IR__Load___Read,
  input  [1:0] CTRL_GPR__Read___Write___Clear,
  input  [3:0] Input_MEM,
  input  [1:0] Address_GPR,
  output [3:0] Output
);

  wire [3:0] demultiplexer_1_out_0, demultiplexer_1_out_1, gpr_1_output, ir_1_p4, pc_1_address_output,
       registers_dram_1_output;

  Registers_DRAM registers_dram_1 (
    .Data(Input_MEM), .Read___Write(CTRL_DRAM__Read___Write), .clk(clk), .Address(pc_1_address_output),
    .Output(registers_dram_1_output));
  PC pc_1 (
    .CTRL__Inc___Write___Reset(CTRL_PC__Inc___Write___Reset), .Manual_Load(Manual_Address_Input_PC),
    .clk(clk), .Address_Output(pc_1_address_output));
  Demultiplexer #(.Bits(4)) demultiplexer_1 (
    .sel(Chip_Select__IR___GPR), .in(registers_dram_1_output), .out_0(demultiplexer_1_out_0),
    .out_1(demultiplexer_1_out_1));
  // IR ir_1: pin names not known; wires that end beside it: CTRL_IR__Load___Read, clk, demultiplexer_1_out_0, ir_1_p4
  GPR gpr_1 (
    .CTRL__Read___Write___Clear(CTRL_GPR__Read___Write___Clear), .clk(clk), .Input(demultiplexer_1_out_1),
    .Address(Address_GPR), .Output(gpr_1_output));
  Multiplexer #(.Bits(4)) multiplexer_1 (
    .sel(Chip_Select__IR___GPR), .in_0(ir_1_p4), .in_1(gpr_1_output), .out(Output));
endmodule
