// Digital circuit GPR.dig as structural Verilog
module GPR (
  input  [1:0] CTRL__Read___Write___Clear,
  input  clk,
  input  [3:0] Input,
  input  [1:0] Address,
  output [3:0] Output
);

  wire demultiplexer_1_out_0, demultiplexer_1_out_1, demultiplexer_1_out_2, demultiplexer_1_out_3;
  wire [3:0] multiplexer_1_out, not_1_out, R_0_p3, R_1_p3, R_2_p3, R_3_p3;

  assign not_1_out = ~4'b0000;  // Not not_1, 4 bits wide
  Demultiplexer #(.Selector_Bits(2)) demultiplexer_1 (
    .sel(Address), .in(clk), .out_0(demultiplexer_1_out_0), .out_1(demultiplexer_1_out_1),
    .out_2(demultiplexer_1_out_2), .out_3(demultiplexer_1_out_3));
  Multiplexer #(.Bits(4), .Selector_Bits(2)) multiplexer_1 (
    .sel(CTRL__Read___Write___Clear), .in_0(Output), .in_1(Input), .in_2(4'b0000), .in_3(not_1_out),
    .out(multiplexer_1_out));
  // _4_bit_register R_3: pin names not known; wires that end beside it: multiplexer_1_out, demultiplexer_1_out_3, R_3_p3
  // _4_bit_register R_2: pin names not known; wires that end beside it: multiplexer_1_out, demultiplexer_1_out_2, R_2_p3
  // _4_bit_register R_1: pin names not known; wires that end beside it: multiplexer_1_out, demultiplexer_1_out_1, R_1_p3
  // _4_bit_register R_0: pin names not known; wires that end beside it: multiplexer_1_out, demultiplexer_1_out_0, R_0_p3
  Multiplexer #(.Bits(4), .Selector_Bits(2)) multiplexer_2 (
    .sel(Address), .in_0(R_0_p3), .in_1(R_1_p3), .in_2(R_2_p3), .in_3(R_3_p3), .out(Output));
endmodule
