// Digital circuit PC.dig as structural Verilog
module PC (
  input  [1:0] CTRL__Inc___Write___Reset,
  input  [3:0] Manual_Load,
  input  clk,
  output [3:0] Address_Output
);

  wire [3:0] _4_bit_adder_1_p3, multiplexer_1_out, not_1_out;

  // _4_bit_adder _4_bit_adder_1: pin names not known; wires that end beside it: Address_Output, 4'b0001, _4_bit_adder_1_p3
  Multiplexer #(.Bits(4), .Selector_Bits(2)) multiplexer_1 (
    .sel(CTRL__Inc___Write___Reset), .in_0(_4_bit_adder_1_p3), .in_1(Manual_Load), .in_2(4'b0000),
    .in_3(not_1_out), .out(multiplexer_1_out));
  assign not_1_out = ~4'b0000;  // Not not_1, 4 bits wide
  // _4_bit_register _4_bit_register_1: pin names not known; wires that end beside it: multiplexer_1_out, clk, Address_Output
endmodule
