// Digital circuit Registers_DRAM.dig as structural Verilog
module Registers_DRAM (
  input  [3:0] Data,
  input  Read___Write,
  input  clk,
  input  [3:0] Address,
  output [3:0] Output
);

  wire demultiplexer_1_out_0, demultiplexer_1_out_1, demultiplexer_1_out_2, demultiplexer_1_out_3,
       demultiplexer_1_out_4, demultiplexer_1_out_5, demultiplexer_1_out_6, demultiplexer_1_out_7,
       demultiplexer_1_out_8, demultiplexer_1_out_9, demultiplexer_1_out_10, demultiplexer_1_out_11,
       demultiplexer_1_out_12, demultiplexer_1_out_13, demultiplexer_1_out_14, demultiplexer_1_out_15;
  wire [3:0] multiplexer_1_out, R_0_p3, R_1_p3, R_2_p3, R_3_p3, R_4_p3, R_5_p3, R_6_p3, R_7_p3, R_8_p3,
       R_9_p3, R_10_p3, R_11_p3, R_12_p3, R_13_p3, R_14_p3, R_15_p3;

  Demultiplexer #(.Selector_Bits(4)) demultiplexer_1 (
    .sel(Address), .in(clk), .out_0(demultiplexer_1_out_0), .out_1(demultiplexer_1_out_1),
    .out_2(demultiplexer_1_out_2), .out_3(demultiplexer_1_out_3), .out_4(demultiplexer_1_out_4),
    .out_5(demultiplexer_1_out_5), .out_6(demultiplexer_1_out_6), .out_7(demultiplexer_1_out_7),
    .out_8(demultiplexer_1_out_8), .out_9(demultiplexer_1_out_9), .out_10(demultiplexer_1_out_10),
    .out_11(demultiplexer_1_out_11), .out_12(demultiplexer_1_out_12), .out_13(demultiplexer_1_out_13),
    .out_14(demultiplexer_1_out_14), .out_15(demultiplexer_1_out_15));
  Multiplexer #(.Bits(4)) multiplexer_1 (.sel(Read___Write), .in_0(Output), .in_1(Data), .out(multiplexer_1_out));
  // _4_bit_register R_15: pin names not known; wires that end beside it: multiplexer_1_out, demultiplexer_1_out_15, R_15_p3
  // _4_bit_register R_14: pin names not known; wires that end beside it: multiplexer_1_out, demultiplexer_1_out_14, R_14_p3
  // _4_bit_register R_13: pin names not known; wires that end beside it: multiplexer_1_out, demultiplexer_1_out_13, R_13_p3
  // _4_bit_register R_12: pin names not known; wires that end beside it: multiplexer_1_out, demultiplexer_1_out_12, R_12_p3
  // _4_bit_register R_11: pin names not known; wires that end beside it: multiplexer_1_out, demultiplexer_1_out_11, R_11_p3
  // _4_bit_register R_10: pin names not known; wires that end beside it: multiplexer_1_out, demultiplexer_1_out_10, R_10_p3
  // _4_bit_register R_9: pin names not known; wires that end beside it: multiplexer_1_out, demultiplexer_1_out_9, R_9_p3
  // _4_bit_register R_8: pin names not known; wires that end beside it: multiplexer_1_out, demultiplexer_1_out_8, R_8_p3
  // _4_bit_register R_7: pin names not known; wires that end beside it: multiplexer_1_out, demultiplexer_1_out_7, R_7_p3
  // _4_bit_register R_6: pin names not known; wires that end beside it: multiplexer_1_out, demultiplexer_1_out_6, R_6_p3
  // _4_bit_register R_5: pin names not known; wires that end beside it: multiplexer_1_out, demultiplexer_1_out_5, R_5_p3
  // _4_bit_register R_4: pin names not known; wires that end beside it: multiplexer_1_out, demultiplexer_1_out_4, R_4_p3
  // _4_bit_register R_3: pin names not known; wires that end beside it: multiplexer_1_out, demultiplexer_1_out_3, R_3_p3
  // _4_bit_register R_2: pin names not known; wires that end beside it: multiplexer_1_out, demultiplexer_1_out_2, R_2_p3
  // _4_bit_register R_1: pin names not known; wires that end beside it: multiplexer_1_out, demultiplexer_1_out_1, R_1_p3
  // _4_bit_register R_0: pin names not known; wires that end beside it: multiplexer_1_out, demultiplexer_1_out_0, R_0_p3
  Multiplexer #(.Selector_Bits(4), .Bits(4)) multiplexer_2 (
    .sel(Address), .in_0(R_0_p3), .in_1(R_1_p3), .in_2(R_2_p3), .in_3(R_3_p3), .in_4(R_4_p3), .in_5(R_5_p3),
    .in_6(R_6_p3), .in_7(R_7_p3), .in_8(R_8_p3), .in_9(R_9_p3), .in_10(R_10_p3), .in_11(R_11_p3),
    .in_12(R_12_p3), .in_13(R_13_p3), .in_14(R_14_p3), .in_15(R_15_p3), .out(Output));
endmodule
